# Fritzing sketch Hamra (saved by Fritzing 0.9.10b)

parts:
  Part1 = Arduino Leonardo (Rev3b)
  JOY1 = Adafruit Arcade Joystick
  S1 = Round Pushbutton
  JOY2 = Adafruit Arcade Joystick
  S2 = Round Pushbutton
  S3 = Round Pushbutton
  S4 = Round Pushbutton
  S5 = Round Pushbutton

nets:
  N1: Part1.D1/TX, S5.leg0
  N2: Part1.D2/SDA, JOY1.E
  N3: Part1.D3_PWM/SCL, JOY1.W
  N4: Part1.D4/A6, JOY1.S
  N5: Part1.D5_PWM, JOY1.N
  N6: Part1.D6_PWM/A7, S1.leg0
  N7: Part1.D7, S4.leg0
  N8: Part1.GND, JOY1.COM, S1.leg1
  N9: Part1.D8/A8, JOY2.E
  N10: Part1.D9_PWM/A9, JOY2.W
  N11: Part1.D10_PWM/A10, JOY2.S
  N12: Part1.D11_PWM, JOY2.N
  N13: Part1.D12/A11, S2.leg0
  N14: Part1.D13_PWM, S3.leg1
  N15: JOY2.COM, S2.leg1
